// Digital circuit AND6Bit.dig as structural Verilog
module AND6Bit (
  input  [5:0] X_5_0,
  input  [5:0] Y_5_0,
  output [5:0] AND_5_0
);

  and and_1 (AND_5_0[5], X_5_0[5], Y_5_0[5]);
  and and_2 (AND_5_0[4], X_5_0[4], Y_5_0[4]);
  and and_3 (AND_5_0[3], X_5_0[3], Y_5_0[3]);
  and and_4 (AND_5_0[2], X_5_0[2], Y_5_0[2]);
  and and_5 (AND_5_0[1], X_5_0[1], Y_5_0[1]);
  and and_6 (AND_5_0[0], X_5_0[0], Y_5_0[0]);
endmodule
