// Digital circuit CPU_6Bit.dig as structural Verilog
module CPU_6Bit (
  input  [3:0] RA2_3_0,
  input  [3:0] WA_3_0,
  input  [14:0] WD_14_0,
  input  WE,
  input  CLK,
  input  PC_EN,
  output [14:0] RD2_14_0,
  output [5:0] R_5_0
);

  wire alu6bit_1_cf, alu6bit_1_sf, alu6bit_1_zf, CF, CPU_CLK, Imm_sel, JMP_sel, SF, WE_reg, ZF;
  wire [1:0] DontCare_ImmMode, OP;
  wire [3:0] multiplexer_1_out, pc4bit_1_o_3_0, pc_adder4bit_1_o_3_0;
  wire [3:1] JMP_addr;
  wire [3:2] Opcode;
  wire [5:0] multiplexer_2_out, regset_6bit_5reg_1_a_5_0, regset_6bit_5reg_1_b_5_0;
  wire [5:5] IMM_value;
  wire [6:2] DontCare_JumpMode;

  Multiplexer #(.Bits(4)) multiplexer_1 (
    .sel(JMP_sel), .in_0(pc_adder4bit_1_o_3_0), .in_1({JMP_addr, IMM_value[5]}), .out(multiplexer_1_out));
  PC4Bit pc4bit_1 (.I_3_0(multiplexer_1_out), .CLK(CPU_CLK), .O_3_0(pc4bit_1_o_3_0));
  PC_ADDER4Bit pc_adder4bit_1 (.I_3_0(pc4bit_1_o_3_0), .O_3_0(pc_adder4bit_1_o_3_0));
  and and_1 (CPU_CLK, PC_EN, CLK);
  SRAM9x15 sram9x15_1 (
    .RA1_3_0(pc4bit_1_o_3_0), .RA2_3_0(RA2_3_0), .WA_3_0(WA_3_0), .WD_14_0(WD_14_0), .WE(WE), .CLK(CLK),
    .RD1_14_0({Opcode, OP, JMP_addr, IMM_value[5], DontCare_JumpMode, DontCare_ImmMode}), .RD2_14_0(RD2_14_0));
  REGSET_6Bit_5Reg regset_6bit_5reg_1 (
    .Wr_2_0(JMP_addr), .CLK(CPU_CLK), .WE(WE_reg), .Wrd_5_0(R_5_0), .Ra_2_0(JMP_addr),
    .Rb_2_0({IMM_value[5], DontCare_JumpMode[6:5]}), .A_5_0(regset_6bit_5reg_1_a_5_0),
    .B_5_0(regset_6bit_5reg_1_b_5_0));
  ALU6Bit alu6bit_1 (
    .A_5_0(regset_6bit_5reg_1_a_5_0), .B_5_0(multiplexer_2_out), .OP_1_0(OP), .CF(alu6bit_1_cf),
    .SF(alu6bit_1_sf), .ZF(alu6bit_1_zf), .R_5_0(R_5_0));
  FlagRegister flagregister_1 (
    .CLK(CPU_CLK), .CF_in(alu6bit_1_cf), .SF_in(alu6bit_1_sf), .ZF_in(alu6bit_1_zf), .CF(CF), .SF(SF), .ZF(ZF));
  ControlUnit controlunit_1 (
    .Opcode({Opcode, OP}), .ZF(ZF), .SF(SF), .OP(OP), .Reg_en(WE_reg), .Imm_sel(Imm_sel), .JMP_sel(JMP_sel));
  Multiplexer #(.Bits(6)) multiplexer_2 (
    .sel(Imm_sel), .in_0(regset_6bit_5reg_1_b_5_0), .in_1({IMM_value[5], DontCare_JumpMode}),
    .out(multiplexer_2_out));

  // Other names for the same wires on the sheet: DontCare_JumpMode[1:0] = DontCare_ImmMode;
  //   DontCare_RegMode[4:0] = {DontCare_JumpMode[4:2], DontCare_ImmMode}; IMM_value[4:0] = DontCare_JumpMode;
  //   Rb[2:0] = {IMM_value[5], DontCare_JumpMode[6:5]}; JMP_addr[0] = IMM_value[5]; Ra[2:0] = JMP_addr;
  //   Opcode[1:0] = OP; typeOfOP[1:0] = Opcode; RA2[3:0] = RA2_3_0; RD2[14:0] = RD2_14_0; WA[3:0] = WA_3_0;
  //   WD[14:0] = WD_14_0

  // Notes on the sheet:
  //   Register Mode (type of op=00) : 2bit (type of op)+ 2bit (op) + 3 bit (Reg1) + 3 bit (Reg1) + 5 bit (don't care)
  //   Immediate Mode (type of op=01) : 2bit (type of op)+ 2bit (op) + 3 bit (Reg1) + 6 bit (Imm value) + 2 bit (don't care)
  //   Jump Mode (type of op=10) : 2bit (type of op)+ 2bit (op) + 4 bit (Addr_of_sram) + 7 bit (don't care)
  //   JMP(OP=00), JL(OP=01)
  //   AND(OP= 00), ADD(OP=01), ROR(OP=10)
  //   START: ADD R1, 5 => 010100100010100
  //   ADD R2, 0 => 010101000000000
  //   AND R1, R2 => 000000101000000
  //   JL START=> 100100010000000
  //   START: ADD R1, 0 => 010100100000000
  //   ADD R2, 1 => 010101000000100
  //   AND R1, R2 => 000000101000000
  //   JMP START=> 100000010000000
endmodule
