// Digital circuit ControlUnit.dig as structural Verilog
module ControlUnit (
  input  [3:0] Opcode,
  input  ZF,
  input  SF,
  output [1:0] OP,
  output Reg_en,
  output Imm_sel,
  output JMP_sel
);

  wire and_1_out, and_3_out, and_4_out, and_5_out, or_1_out;

  and and_1 (and_1_out, ~Opcode[2], ~Opcode[3]);  // And
  and and_2 (Imm_sel, Opcode[2], ~Opcode[3]);  // And
  and and_3 (and_3_out, ~Opcode[2], Opcode[3]);  // And
  and and_4 (and_4_out, ~Opcode[0], ~Opcode[1]);  // And
  and and_5 (and_5_out, Opcode[0], ~Opcode[1], ZF, ~SF);  // And
  or or_1 (or_1_out, and_4_out, and_5_out);
  or or_2 (Reg_en, and_1_out, Imm_sel);
  and and_6 (JMP_sel, and_3_out, or_1_out);

  assign OP = Opcode[1:0];
endmodule
