// Digital circuit FA1Bit.dig as structural Verilog
module FA1Bit (
  input  X,
  input  Y,
  input  Cin,
  output S,
  output Cout
);

  wire and_1_out, and_2_out, xor_1_out;

  xor xor_1 (xor_1_out, X, Y);
  and and_1 (and_1_out, X, Y);
  and and_2 (and_2_out, xor_1_out, Cin);
  xor xor_2 (S, xor_1_out, Cin);
  or or_1 (Cout, and_2_out, and_1_out);
endmodule
