// Digital circuit FA6Bit.dig as structural Verilog
module FA6Bit (
  input  [5:0] X_5_0,
  input  [5:0] Y_5_0,
  output [5:0] S_5_0,
  output C
);

  wire fa1bit_2_cout, fa1bit_3_cout, fa1bit_4_cout, fa1bit_5_cout, fa1bit_6_cout;

  FA1Bit fa1bit_1 (.Y(Y_5_0[5]), .X(X_5_0[5]), .Cin(fa1bit_2_cout), .S(S_5_0[5]), .Cout(C));
  FA1Bit fa1bit_2 (.Y(Y_5_0[4]), .X(X_5_0[4]), .Cin(fa1bit_3_cout), .S(S_5_0[4]), .Cout(fa1bit_2_cout));
  FA1Bit fa1bit_3 (.Y(Y_5_0[3]), .X(X_5_0[3]), .Cin(fa1bit_4_cout), .S(S_5_0[3]), .Cout(fa1bit_3_cout));
  FA1Bit fa1bit_4 (.Y(Y_5_0[2]), .X(X_5_0[2]), .Cin(fa1bit_5_cout), .S(S_5_0[2]), .Cout(fa1bit_4_cout));
  FA1Bit fa1bit_5 (.Y(Y_5_0[1]), .X(X_5_0[1]), .Cin(fa1bit_6_cout), .S(S_5_0[1]), .Cout(fa1bit_5_cout));
  FA1Bit fa1bit_6 (.Y(Y_5_0[0]), .X(X_5_0[0]), .Cin(1'b0), .S(S_5_0[0]), .Cout(fa1bit_6_cout));
endmodule
