// Digital circuit FlagRegister.dig as structural Verilog
module FlagRegister (
  input  CLK,
  input  CF_in,
  input  SF_in,
  input  ZF_in,
  output CF,
  output SF,
  output ZF
);

  REG1Bit reg1bit_1 (.Din(CF_in), .Sel(1'b1), .CLK(CLK), .Dout(CF));
  REG1Bit reg1bit_2 (.Din(SF_in), .Sel(1'b1), .CLK(CLK), .Dout(SF));
  REG1Bit reg1bit_3 (.Din(ZF_in), .Sel(1'b1), .CLK(CLK), .Dout(ZF));
endmodule
