// Digital circuit PC4Bit.dig as structural Verilog
module PC4Bit (
  input  [3:0] I_3_0,
  input  CLK,
  output [3:0] O_3_0
);

  wire [5:4] reg6bit_1_dout;

  REG6Bit reg6bit_1 (.Din({2'b00, I_3_0}), .Sel(1'b1), .CLK(CLK), .Dout({reg6bit_1_dout, O_3_0}));
endmodule
