// Digital circuit PC_ADDER4Bit.dig as structural Verilog
module PC_ADDER4Bit (
  input  [3:0] I_3_0,
  output [3:0] O_3_0
);

  Add #(.Bits(4)) add_1 (.a(I_3_0), .b(4'b0001), .c_i(1'b0), .s(O_3_0));  // open: c_o
endmodule
