// Digital circuit REG6Bit.dig as structural Verilog
module REG6Bit (
  input  [5:0] Din,
  input  Sel,
  input  CLK,
  output [5:0] Dout
);

  REG1Bit reg1bit_1 (.Din(Din[0]), .Sel(Sel), .CLK(CLK), .Dout(Dout[0]));
  REG1Bit reg1bit_2 (.Din(Din[1]), .Sel(Sel), .CLK(CLK), .Dout(Dout[1]));
  REG1Bit reg1bit_3 (.Din(Din[2]), .Sel(Sel), .CLK(CLK), .Dout(Dout[2]));
  REG1Bit reg1bit_4 (.Din(Din[3]), .Sel(Sel), .CLK(CLK), .Dout(Dout[3]));
  REG1Bit reg1bit_5 (.Din(Din[4]), .Sel(Sel), .CLK(CLK), .Dout(Dout[4]));
  REG1Bit reg1bit_6 (.Din(Din[5]), .Sel(Sel), .CLK(CLK), .Dout(Dout[5]));
endmodule
