// Digital circuit REGSET_6Bit_5Reg.dig as structural Verilog
module REGSET_6Bit_5Reg (
  input  [2:0] Wr_2_0,
  input  WE,
  input  [5:0] Wrd_5_0,
  input  CLK,
  input  [2:0] Ra_2_0,
  input  [2:0] Rb_2_0,
  output [5:0] A_5_0,
  output [5:0] B_5_0
);

  wire R0, R1, R2, R3, R4, Reg0, Reg1, Reg2, Reg3, Reg4;
  wire [5:0] D0, D1, D2, D3, D4;

  Decoder #(.Selector_Bits(3)) decoder_1 (
    .sel(Wr_2_0), .out_0(R0), .out_1(R1), .out_2(R2), .out_3(R3), .out_4(R4));  // open: out_5, out_6, out_7
  and and_1 (Reg0, R0, WE);
  and and_2 (Reg1, R1, WE);
  and and_3 (Reg2, R2, WE);
  and and_4 (Reg3, R3, WE);
  and and_5 (Reg4, R4, WE);
  REG6Bit reg6bit_1 (.Din(Wrd_5_0), .Sel(Reg0), .CLK(CLK), .Dout(D0));
  REG6Bit reg6bit_2 (.Din(Wrd_5_0), .Sel(Reg1), .CLK(CLK), .Dout(D1));
  REG6Bit reg6bit_3 (.Din(Wrd_5_0), .Sel(Reg2), .CLK(CLK), .Dout(D2));
  REG6Bit reg6bit_4 (.Din(Wrd_5_0), .Sel(Reg3), .CLK(CLK), .Dout(D3));
  REG6Bit reg6bit_5 (.Din(Wrd_5_0), .Sel(Reg4), .CLK(CLK), .Dout(D4));
  Multiplexer #(.Selector_Bits(3), .Bits(6)) multiplexer_1 (
    .sel(Ra_2_0), .in_0(D0), .in_1(D1), .in_2(D2), .in_3(D3), .in_4(D4), .in_5({6{1'b0}}), .in_6({6{1'b0}}),
    .in_7({6{1'b0}}), .out(A_5_0));
  Multiplexer #(.Selector_Bits(3), .Bits(6)) multiplexer_2 (
    .sel(Rb_2_0), .in_0(D0), .in_1(D1), .in_2(D2), .in_3(D3), .in_4(D4), .in_5({6{1'b0}}), .in_6({6{1'b0}}),
    .in_7({6{1'b0}}), .out(B_5_0));

  // Other names for the same wires on the sheet: A[5:0] = A_5_0; B[5:0] = B_5_0; Ra[2:0] = Ra_2_0; Rb[2:0] = Rb_2_0;
  //   REG_en = WE; WrD[5:0] = Wrd_5_0
endmodule
