// Digital circuit ROR6Bit.dig as structural Verilog
module ROR6Bit (
  input  [5:0] Sel_5_0,
  input  [5:0] X_5_0,
  output [5:0] ROR_5_0
);

  wire [5:0] multiplexer_1_out;
  wire [5:5] nor_1_out;

  nor nor_1 (nor_1_out[5], Sel_5_0[3], Sel_5_0[4], Sel_5_0[5]);
  Multiplexer #(.Selector_Bits(3)) multiplexer_1 (
    .sel(Sel_5_0[2:0]), .in_0(X_5_0[5]), .in_1(X_5_0[0]), .in_2(X_5_0[1]), .in_3(X_5_0[2]), .in_4(X_5_0[3]),
    .in_5(X_5_0[4]), .in_6(1'b0), .in_7(1'b0), .out(multiplexer_1_out[5]));
  Multiplexer #(.Selector_Bits(3)) multiplexer_2 (
    .sel(Sel_5_0[2:0]), .in_0(X_5_0[4]), .in_1(X_5_0[5]), .in_2(X_5_0[0]), .in_3(X_5_0[1]), .in_4(X_5_0[2]),
    .in_5(X_5_0[3]), .in_6(1'b0), .in_7(1'b0), .out(multiplexer_1_out[4]));
  Multiplexer #(.Selector_Bits(3)) multiplexer_3 (
    .sel(Sel_5_0[2:0]), .in_0(X_5_0[3]), .in_1(X_5_0[4]), .in_2(X_5_0[5]), .in_3(X_5_0[0]), .in_4(X_5_0[1]),
    .in_5(X_5_0[2]), .in_6(1'b0), .in_7(1'b0), .out(multiplexer_1_out[3]));
  Multiplexer #(.Selector_Bits(3)) multiplexer_4 (
    .sel(Sel_5_0[2:0]), .in_0(X_5_0[2]), .in_1(X_5_0[3]), .in_2(X_5_0[4]), .in_3(X_5_0[5]), .in_4(X_5_0[0]),
    .in_5(X_5_0[1]), .in_6(1'b0), .in_7(1'b0), .out(multiplexer_1_out[2]));
  Multiplexer #(.Selector_Bits(3)) multiplexer_5 (
    .sel(Sel_5_0[2:0]), .in_0(X_5_0[1]), .in_1(X_5_0[2]), .in_2(X_5_0[3]), .in_3(X_5_0[4]), .in_4(X_5_0[5]),
    .in_5(X_5_0[0]), .in_6(1'b0), .in_7(1'b0), .out(multiplexer_1_out[1]));
  Multiplexer #(.Selector_Bits(3)) multiplexer_6 (
    .sel(Sel_5_0[2:0]), .in_0(X_5_0[0]), .in_1(X_5_0[1]), .in_2(X_5_0[2]), .in_3(X_5_0[3]), .in_4(X_5_0[4]),
    .in_5(X_5_0[5]), .in_6(1'b0), .in_7(1'b0), .out(multiplexer_1_out[0]));
  assign ROR_5_0 = multiplexer_1_out & {6{nor_1_out[5]}};  // And and_1, 6 bits wide

  // Other names for the same wires on the sheet: X0 = X_5_0[0]; X1 = X_5_0[1]; X2 = X_5_0[2]; x3 = X_5_0[3];
  //   X4 = X_5_0[4]; X5 = X_5_0[5]
endmodule
