// Digital circuit SRAM9x15.dig as structural Verilog
module SRAM9x15 (
  input  [3:0] RA1_3_0,
  input  [3:0] RA2_3_0,
  input  [3:0] WA_3_0,
  input  [14:0] WD_14_0,
  input  WE,
  input  CLK,
  output [14:0] RD1_14_0,
  output [14:0] RD2_14_0
);

  wire RAi0, RAi1, RAi2, RAi3, RAi4, RAi5, RAi6, RAi7, RAi8, RAii0, RAii1, RAii2, RAii3, RAii4, RAii5, RAii6,
       RAii7, RAii8, W0, W1, W2, W3, W5, W6, W7, W8, W9, WA0, WA1, WA2, WA3, WA4, WA5, WA6, WA7, WA8;
  wire [14:0] RDi0, RDi1, RDi2, RDi3, RDi4, RDi5, RDi6, RDi7, RDi8, RDii0, RDii1, RDii2, RDii3, RDii4, RDii5,
       RDii6, RDii7, RDii8;

  Decoder #(.Selector_Bits(4)) decoder_1 (
    .sel(RA1_3_0), .out_0(RAi0), .out_1(RAi1), .out_2(RAi2), .out_3(RAi3), .out_4(RAi4), .out_5(RAi5),
    .out_6(RAi6), .out_7(RAi7), .out_8(RAi8));  // open: out_9, out_10, out_11, out_12, out_13, out_14, out_15
  Decoder #(.Selector_Bits(4)) decoder_2 (
    .sel(RA2_3_0), .out_0(RAii0), .out_1(RAii1), .out_2(RAii2), .out_3(RAii3), .out_4(RAii4), .out_5(RAii5),
    .out_6(RAii6), .out_7(RAii7), .out_8(RAii8));  // open: out_9, out_10, out_11, out_12, out_13, out_14, out_15
  Decoder #(.Selector_Bits(4)) decoder_3 (
    .sel(WA_3_0), .out_0(WA0), .out_1(WA1), .out_2(WA2), .out_3(WA3), .out_4(WA4), .out_5(WA5), .out_6(WA6),
    .out_7(WA7), .out_8(WA8));  // open: out_9, out_10, out_11, out_12, out_13, out_14, out_15
  and and_1 (W0, WA0, WE);
  and and_2 (W1, WA1, WE);
  and and_3 (W2, WA2, WE);
  and and_4 (W3, WA3, WE);
  and and_5 (W5, WA4, WE);
  and and_6 (W6, WA5, WE);
  and and_7 (W7, WA6, WE);
  and and_8 (W8, WA7, WE);
  and and_9 (W9, WA8, WE);
  SRAM1x15 sram1x15_1 (
    .RS1(RAi0), .RS2(RAii0), .WS(W0), .WD_14_0(WD_14_0), .CLK(CLK), .RD1_14_0(RDi0), .RD2_14_0(RDii0));
  SRAM1x15 sram1x15_2 (
    .RS1(RAi3), .RS2(RAii3), .WS(W3), .WD_14_0(WD_14_0), .CLK(CLK), .RD1_14_0(RDi3), .RD2_14_0(RDii3));
  SRAM1x15 sram1x15_3 (
    .RS1(RAi6), .RS2(RAii6), .WS(W7), .WD_14_0(WD_14_0), .CLK(CLK), .RD1_14_0(RDi6), .RD2_14_0(RDii6));
  SRAM1x15 sram1x15_4 (
    .RS1(RAi1), .RS2(RAii1), .WS(W1), .WD_14_0(WD_14_0), .CLK(CLK), .RD1_14_0(RDi1), .RD2_14_0(RDii1));
  SRAM1x15 sram1x15_5 (
    .RS1(RAi4), .RS2(RAii4), .WS(W5), .WD_14_0(WD_14_0), .CLK(CLK), .RD1_14_0(RDi4), .RD2_14_0(RDii4));
  SRAM1x15 sram1x15_6 (
    .RS1(RAi7), .RS2(RAii7), .WS(W8), .WD_14_0(WD_14_0), .CLK(CLK), .RD1_14_0(RDi7), .RD2_14_0(RDii7));
  SRAM1x15 sram1x15_7 (
    .RS1(RAi2), .RS2(RAii2), .WS(W2), .WD_14_0(WD_14_0), .CLK(CLK), .RD1_14_0(RDi2), .RD2_14_0(RDii2));
  SRAM1x15 sram1x15_8 (
    .RS1(RAi5), .RS2(RAii5), .WS(W6), .WD_14_0(WD_14_0), .CLK(CLK), .RD1_14_0(RDi5), .RD2_14_0(RDii5));
  SRAM1x15 sram1x15_9 (
    .RS1(RAi8), .RS2(RAii8), .WS(W9), .WD_14_0(WD_14_0), .CLK(CLK), .RD1_14_0(RDi8), .RD2_14_0(RDii8));
  assign RD1_14_0 = RDi0 | RDi1 | RDi2 | RDi3 | RDi4 | RDi5 | RDi6 | RDi7 | RDi8;  // Or or_1, 15 bits wide
  assign RD2_14_0 = RDii0 | RDii1 | RDii2 | RDii3 | RDii4 | RDii5 | RDii6 | RDii7 | RDii8;  // Or or_2, 15 bits wide

  // Other names for the same wires on the sheet: WD[14:0] = WD_14_0
endmodule
